# Fritzing sketch PiZero-RTC-nrf24-rain-temperature-v2 (saved by Fritzing 0.9.3b)
perfboards: 2

parts:
  Raspberry_Pi_Zero2 = Raspberry Pi Zero
  ZS-042_RTC5 = ZS-042 RTC Module
  Part7 = NRF24L01+ Breakout Board
  YL-83_-_Control_Board3 = YL-83 Rain Sensor - Control Board
  YL-83_-_Detection_Board3 = YL-83 Rain Sensor - Detection Board
  DS4 = DS18B20 1-Wire Temperature Sensor Probe Cable
  R11 = Resistor [tolerance=±5% resistance=4.7k package=THT]
  Raspberry_Pi_Zero3 = Raspberry Pi Zero
  YL-83_-_Control_Board4 = YL-83 Rain Sensor - Control Board
  YL-83_-_Detection_Board4 = YL-83 Rain Sensor - Detection Board
  Part8 = NRF24L01+ Breakout Board  # not connected
  DS5 = DS18B20 1-Wire Temperature Sensor Probe Cable  # not connected
  R12 = Resistor [tolerance=±5% resistance=4.7k package=THT]  # not connected
  J1 = male pin header, 5 pins [form="♂ (male)"]
  J2 = male pin header, 2 pins [form="♂ (male)"]
  J3 = male pin header, 3 pins [form="♂ (male)"]
  J4 = female pin header, 4 pins [form="♀ (female)"]  # not connected

nets:
  3V3: Raspberry_Pi_Zero2.3v3, Raspberry_Pi_Zero2.3V3, ZS-042_RTC5.VCC, Part7.VCC
  N1: Raspberry_Pi_Zero2.GPIO2, ZS-042_RTC5.SDA
  N2: Raspberry_Pi_Zero2.GPIO3, ZS-042_RTC5.SCL
  N3: Raspberry_Pi_Zero2.GPIO4, DS4.DQ
  GND: Raspberry_Pi_Zero2.GND, ZS-042_RTC5.GND, Part7.GND, YL-83_-_Control_Board3.GND, DS4.GND
  N4: Raspberry_Pi_Zero2.GPIO10, Part7.MISO
  N5: Raspberry_Pi_Zero2.GPIO9, Part7.MOSI
  N6: Raspberry_Pi_Zero2.GPIO11, Part7.SCK
  N7: Raspberry_Pi_Zero2.GPIO7, Part7.CE
  N8: Raspberry_Pi_Zero2.GPIO8, Part7.CS
  5V: Raspberry_Pi_Zero2.5V, DS4.VDD, R11.Pin_1
  N9: YL-83_-_Control_Board3.POS, YL-83_-_Detection_Board3.POS
  N10: YL-83_-_Control_Board3.NEG, YL-83_-_Detection_Board3.NEG
  3V3_2: Raspberry_Pi_Zero3.3v3, Raspberry_Pi_Zero3.3V3, J1.pin1
  N11: Raspberry_Pi_Zero3.GPIO2, J1.pin2
  N12: Raspberry_Pi_Zero3.GPIO3, J1.pin3
  N13: Raspberry_Pi_Zero3.GND, J1.pin5, J2.pin2
  N14: Raspberry_Pi_Zero3.5V, J2.pin1, J3.pin1
  N15: YL-83_-_Control_Board4.POS, YL-83_-_Detection_Board4.POS
  N16: YL-83_-_Control_Board4.NEG, YL-83_-_Detection_Board4.NEG

notes:
  ** RTC **
  VCC to 3.3 or 5v
  GND to GND
  SDA to A4
  SCL to A5
  SQW to A2
  ** nRF24 **
  VCC to 3.3v
  GND to GND
  D13 to SCK
  D11 to MOSI
  D12 to MISO
  D10 to CS
  D3 to CE
  IRQ não é usado ainda
  RTC

custom parts:
  YL-83 Rain Sensor - Control Board: The YL-83 is a rain sensor that has more resistance when dry and less resistance when wet. The module runs at 5V.
  YL-83 Rain Sensor - Detection Board: The YL-83 is a rain sensor that has more resistance when dry and less resistance when wet. The module runs at 5V.
