# Fritzing sketch PiZero-RTC-nrf24-rain-temperature-v4 (saved by Fritzing 0.9.3b)
perfboards: 1

parts:
  YL-83_-_Detection_Board4 = YL-83 Rain Sensor - Detection Board
  DS5 = DS18B20 1-Wire Temperature Sensor Probe Cable
  Raspberry_Pi_Zero4 = Raspberry Pi Zero
  YL-83_-_Control_Board5 = YL-83 Rain Sensor - Control Board
  Part9 = NRF24L01+ Breakout Board  # not connected
  R13 = Resistor [tolerance=±5% resistance=4.7k package=THT]
  J7 = male pin header, 5 pins [form="♂ (male)"]
  J8 = female pin header, 4 pins [form="♀ (female)"]
  J9 = male pin header, 3 pins [form="♂ (male)"]
  J10 = female pin header, 4 pins [form="♀ (female)"]
  J11 = female pin header, 4 pins [form="♀ (female)"]
  J12 = male pin header, 3 pins [form="♂ (male)"]

nets:
  N1: YL-83_-_Detection_Board4.POS, YL-83_-_Control_Board5.POS
  N2: YL-83_-_Detection_Board4.NEG, YL-83_-_Control_Board5.NEG
  GND: DS5.GND, Raspberry_Pi_Zero4.GND, J7.pin5, J8.pin2, J9.pin2, J11.pin4, J12.pin2
  N3: DS5.DQ, Raspberry_Pi_Zero4.GPIO4, R13.Pin_0, J9.pin3
  VDD: DS5.VDD, Raspberry_Pi_Zero4.5V, R13.Pin_1, J8.pin1, J9.pin1
  3V3: Raspberry_Pi_Zero4.3v3, Raspberry_Pi_Zero4.3V3, J7.pin1, J10.pin4
  N4: Raspberry_Pi_Zero4.GPIO2, J7.pin2
  N5: Raspberry_Pi_Zero4.GPIO3, J7.pin3
  N6: Raspberry_Pi_Zero4.GPIO22, J11.pin3
  N7: Raspberry_Pi_Zero4.GPIO10, J10.pin2
  N8: Raspberry_Pi_Zero4.GPIO9, J11.pin1
  N9: Raspberry_Pi_Zero4.GPIO11, J11.pin2
  N10: Raspberry_Pi_Zero4.GPIO26, J8.pin3
  N11: Raspberry_Pi_Zero4.GPIO8, J10.pin3

notes:
  RTC
  Serial
  TX
  GND
  RX
  Chuva (1-wire)
  5V
  GND
  Data

custom parts:
  YL-83 Rain Sensor - Detection Board: The YL-83 is a rain sensor that has more resistance when dry and less resistance when wet. The module runs at 5V.
  YL-83 Rain Sensor - Control Board: The YL-83 is a rain sensor that has more resistance when dry and less resistance when wet. The module runs at 5V.
