# Fritzing sketch PiZero-RTC-nrf24-rain-temperature (saved by Fritzing 0.9.3b)
breadboards: 1
perfboards: 1

parts:
  Raspberry_Pi_Zero1 = Raspberry Pi Zero
  ZS-042_RTC4 = ZS-042 RTC Module
  Part6 = NRF24L01+ Breakout Board
  YL-83_-_Control_Board2 = YL-83 Rain Sensor - Control Board
  YL-83_-_Detection_Board2 = YL-83 Rain Sensor - Detection Board
  DS3 = DS18B20 1-Wire Temperature Sensor Probe Cable
  R10 = Resistor [tolerance=±5% resistance=4.7k package=THT]
  Raspberry_Pi_Zero2 = Raspberry Pi Zero
  ZS-042_RTC5 = ZS-042 RTC Module
  Part7 = NRF24L01+ Breakout Board
  YL-83_-_Control_Board3 = YL-83 Rain Sensor - Control Board
  YL-83_-_Detection_Board3 = YL-83 Rain Sensor - Detection Board
  DS4 = DS18B20 1-Wire Temperature Sensor Probe Cable
  R11 = Resistor [tolerance=±5% resistance=4.7k package=THT]

nets:
  3V3: Raspberry_Pi_Zero1.3v3, Raspberry_Pi_Zero1.3V3, ZS-042_RTC4.VCC, Part6.VCC
  N1: Raspberry_Pi_Zero1.GPIO2, ZS-042_RTC4.SDA
  N2: Raspberry_Pi_Zero1.GPIO3, ZS-042_RTC4.SCL
  N3: Raspberry_Pi_Zero1.GPIO4, DS3.DQ, R10.Pin_1
  GND: Raspberry_Pi_Zero1.GND, ZS-042_RTC4.GND, Part6.GND, YL-83_-_Control_Board2.GND, DS3.GND
  N4: Raspberry_Pi_Zero1.GPIO10, Part6.MISO
  N5: Raspberry_Pi_Zero1.GPIO9, Part6.MOSI
  N6: Raspberry_Pi_Zero1.GPIO11, Part6.SCK
  N7: Raspberry_Pi_Zero1.GPIO7, Part6.CE
  N8: Raspberry_Pi_Zero1.GPIO8, Part6.CS
  N9: Raspberry_Pi_Zero1.GPIO23, YL-83_-_Control_Board2.DO
  5V: Raspberry_Pi_Zero1.5V, YL-83_-_Control_Board2.VCC
  N10: YL-83_-_Control_Board2.POS, YL-83_-_Detection_Board2.POS
  N11: YL-83_-_Control_Board2.NEG, YL-83_-_Detection_Board2.NEG
  N12: DS3.VDD, R10.Pin_0
  3V3_2: Raspberry_Pi_Zero2.3v3, Raspberry_Pi_Zero2.3V3, ZS-042_RTC5.VCC, Part7.VCC
  N13: Raspberry_Pi_Zero2.GPIO2, ZS-042_RTC5.SDA
  N14: Raspberry_Pi_Zero2.GPIO3, ZS-042_RTC5.SCL
  N15: Raspberry_Pi_Zero2.GPIO4, DS4.DQ
  GND_2: Raspberry_Pi_Zero2.GND, ZS-042_RTC5.GND, Part7.GND, YL-83_-_Control_Board3.GND, DS4.GND
  N16: Raspberry_Pi_Zero2.GPIO10, Part7.MISO
  N17: Raspberry_Pi_Zero2.GPIO9, Part7.MOSI
  N18: Raspberry_Pi_Zero2.GPIO11, Part7.SCK
  N19: Raspberry_Pi_Zero2.GPIO7, Part7.CE
  N20: Raspberry_Pi_Zero2.GPIO8, Part7.CS
  5V_2: Raspberry_Pi_Zero2.5V, DS4.VDD, R11.Pin_1
  N21: YL-83_-_Control_Board3.POS, YL-83_-_Detection_Board3.POS
  N22: YL-83_-_Control_Board3.NEG, YL-83_-_Detection_Board3.NEG

notes:
  ** RTC **
  VCC to 3.3 or 5v
  GND to GND
  SDA to A4
  SCL to A5
  SQW to A2
  ** nRF24 **
  VCC to 3.3v
  GND to GND
  D13 to SCK
  D11 to MOSI
  D12 to MISO
  D10 to CS
  D3 to CE
  IRQ não é usado ainda

custom parts:
  YL-83 Rain Sensor - Control Board: The YL-83 is a rain sensor that has more resistance when dry and less resistance when wet. The module runs at 5V.
  YL-83 Rain Sensor - Detection Board: The YL-83 is a rain sensor that has more resistance when dry and less resistance when wet. The module runs at 5V.
