# Fritzing sketch Sketch05-pro_mini-semRF24 (saved by Fritzing 0.9.2b)
circuit board: 8.46667cm x 5.64444cm
breadboards: 1

parts:
  R1 = Resistor [tolerance=±5% resistance=4.7k package=THT]
  R2 = Resistor [tolerance=±5% resistance=4.7k package=THT]
  D1 = Rectifier Diode [part_number=1N4342 package="300 mil [THT]"]
  D2 = Rectifier Diode [part_number=1N4342 package="300 mil [THT]"]
  ZS-042_RTC1 = ZS-042 RTC Module
  LM1 = LM2596 [package=multiwatt15]
  Solar_pannel1 = solar_pannel
  Arduino1 = Arduino Pro Mini v13
  Part1 = Arduino Nano (Rev3.0)  # not connected
  Part2 = Arduino Uno (Rev3)  # not connected

nets:
  N1: R1.Pin_0, D2.cathode, Arduino1.A0
  GND: R1.Pin_1, R2.Pin_0, ZS-042_RTC1.GND, LM1.FDBK, Arduino1.GND
  N2: R2.Pin_1, D1.cathode, Arduino1.A1
  N3: D1.anode, Arduino1.D7
  N4: D2.anode, Arduino1.D6_PWM
  VCC: ZS-042_RTC1.VCC, Arduino1.VCC
  N5: ZS-042_RTC1.SDA, Arduino1.A4
  N6: ZS-042_RTC1.SCL, Arduino1.A5
  N7: LM1.Vin, Solar_pannel1.aún_sin_nombre#1
  N8: LM1.Vout, Arduino1.RAW
  N9: LM1.GND, Solar_pannel1.aún_sin_nombre#0

custom parts:
  LM2596: LM2596 switching voltage regulator
  solar_pannel: Solar pannel
