# Fritzing sketch Sketch05-semRF24 (saved by Fritzing 0.9.2b)
breadboards: 1

parts:
  Componente1 = Arduino Uno (Rev3)
  R1 = Resistor [tolerance=±5% resistance=4.7k package=THT]
  R2 = Resistor [tolerance=±5% resistance=4.7k package=THT]
  D1 = Rectifier Diode [part_number=1N4342 package="300 mil [THT]"]
  D2 = Rectifier Diode [part_number=1N4342 package="300 mil [THT]"]
  ZS-042_RTC1 = ZS-042 RTC Module
  LM1 = LM2596 [package=multiwatt15]
  Solar_pannel1 = solar_pannel

nets:
  N1: Componente1.A0, R1.Pin_0, D2.cathode
  N2: Componente1.A1, R2.Pin_1, D1.cathode
  N3: Componente1.A4/SDA, ZS-042_RTC1.SDA
  N4: Componente1.A5/SCL, ZS-042_RTC1.SCL
  N5: Componente1.D6_PWM, D2.anode
  N6: Componente1.D7, D1.anode
  3V3: Componente1.3V3, ZS-042_RTC1.VCC
  GND: Componente1.GND, R1.Pin_1, R2.Pin_0, ZS-042_RTC1.GND, LM1.FDBK
  N7: Componente1.VIN, LM1.Vout
  N8: LM1.Vin, Solar_pannel1.aún_sin_nombre#1
  N9: LM1.GND, Solar_pannel1.aún_sin_nombre#0

custom parts:
  LM2596: LM2596 switching voltage regulator
  solar_pannel: Solar pannel
