# Fritzing sketch Sketch06-nano-chuva-temperatura-semRF24 (saved by Fritzing 0.9.2b)
circuit board: 8.46667cm x 5.64444cm
breadboards: 1

parts:
  R1 = Resistor [tolerance=±5% resistance=4.7k package=THT]
  R2 = Resistor [tolerance=±5% resistance=4.7k package=THT]
  D1 = Rectifier Diode [part_number=1N4342 package="300 mil [THT]"]
  D2 = Rectifier Diode [part_number=1N4342 package="300 mil [THT]"]
  ZS-042_RTC1 = ZS-042 RTC Module
  LM1 = LM2596 [package=multiwatt15]
  Solar_pannel1 = solar_pannel
  Part1 = Arduino Nano (Rev3.0)
  YL-83_-_Control_Board1 = YL-83 Rain Sensor - Control Board
  YL-83_-_Detection_Board1 = YL-83 Rain Sensor - Detection Board
  DS2 = DS18B20 1-Wire Temperature Sensor Probe Cable

nets:
  N1: R1.Pin_0, D2.cathode, Part1.A0
  GND: R1.Pin_1, R2.Pin_0, ZS-042_RTC1.GND, LM1.FDBK, Part1.GND, Part1.A6, YL-83_-_Control_Board1.GND, DS2.GND
  N2: R2.Pin_1, D1.cathode, Part1.A1
  N3: D1.anode, Part1.D7
  N4: D2.anode, Part1.D6
  VCC: ZS-042_RTC1.VCC, Part1.3V3
  N5: ZS-042_RTC1.SDA, Part1.A4
  N6: ZS-042_RTC1.SCL, Part1.A5
  N7: LM1.Vin, Solar_pannel1.aún_sin_nombre#1
  N8: LM1.Vout, Part1.VIN
  N9: LM1.GND, Solar_pannel1.aún_sin_nombre#0
  N10: Part1.D2, YL-83_-_Control_Board1.DO
  N11: Part1.D3, DS2.DQ
  5V: Part1.5V, YL-83_-_Control_Board1.VCC, DS2.VDD
  N12: Part1.A2, YL-83_-_Control_Board1.AO
  N13: YL-83_-_Control_Board1.POS, YL-83_-_Detection_Board1.POS
  N14: YL-83_-_Control_Board1.NEG, YL-83_-_Detection_Board1.NEG

custom parts:
  LM2596: LM2596 switching voltage regulator
  solar_pannel: Solar pannel
  YL-83 Rain Sensor - Control Board: The YL-83 is a rain sensor that has more resistance when dry and less resistance when wet. The module runs at 5V.
  YL-83 Rain Sensor - Detection Board: The YL-83 is a rain sensor that has more resistance when dry and less resistance when wet. The module runs at 5V.
