# Fritzing sketch Sketch08-nano-chuva-temperatura-RTC-SD-semRF24 (saved by Fritzing 0.9.2b)
circuit board: 8.46667cm x 5.64444cm
breadboards: 2

parts:
  R1 = Resistor [tolerance=±5% resistance=4.7k package=THT]
  R2 = Resistor [tolerance=±5% resistance=4.7k package=THT]
  D1 = Rectifier Diode [part_number=1N4342 package="300 mil [THT]"]
  D2 = Rectifier Diode [part_number=1N4342 package="300 mil [THT]"]
  LM1 = LM2596 [package=multiwatt15]
  Solar_pannel1 = solar_pannel
  Part1 = Arduino Nano (Rev3.0)
  YL-83_-_Control_Board2 = YL-83 Rain Sensor - Control Board
  YL-83_-_Detection_Board2 = YL-83 Rain Sensor - Detection Board
  DS3 = DS18B20 1-Wire Temperature Sensor Probe Cable  # not connected
  Part3 = Arduino Cellular Shield  # not connected
  Part4 = MicroSD Card Module  # not connected
  Arduino1 = Arduino Pro Mini v13  # not connected
  Part5 = Arduino Nano (Rev3.0)
  ZS-042_RTC2 = ZS-042 RTC Module
  VCC1 = 4 x AAA Battery Mount
  D3 = Rectifier Diode [part_number=1N4342 package="300 mil [THT]"]
  R3 = Resistor [tolerance=±5% resistance=4.7k package=THT]
  D4 = Rectifier Diode [part_number=1N4342 package="300 mil [THT]"]
  R4 = Resistor [tolerance=±5% resistance=4.7k package=THT]

nets:
  N1: R1.Pin_0, D2.cathode, Part1.A0
  N2: R1.Pin_1, R2.Pin_0
  N3: R2.Pin_1, D1.cathode, Part1.A1
  N4: D1.anode, Part1.D7
  N5: D2.anode, Part1.D6
  N6: LM1.Vin, Solar_pannel1.aún_sin_nombre#1
  N7: LM1.GND, Solar_pannel1.aún_sin_nombre#0
  N8: YL-83_-_Control_Board2.POS, YL-83_-_Detection_Board2.POS
  N9: YL-83_-_Control_Board2.NEG, YL-83_-_Detection_Board2.NEG
  GND: Part5.GND, ZS-042_RTC2.GND, VCC1.-, R3.Pin_1, R4.Pin_0
  N10: Part5.D6, D4.anode
  N11: Part5.D7, D3.anode
  N12: Part5.VIN, VCC1.+
  5V: Part5.5V, ZS-042_RTC2.VCC
  N13: Part5.A5, ZS-042_RTC2.SCL
  N14: Part5.A4, ZS-042_RTC2.SDA
  N15: Part5.A1, D3.cathode, R3.Pin_0
  N16: Part5.A0, D4.cathode, R4.Pin_1

notes:
  ** Micro SD **
  5V to 5V or Vcc
  GND to GND
  D13 to SCK
  D12 to MISO
  D11 to MOSI
  D10 to CS
  ** RTC **
  5V to 5V or Vcc
  GND to GND
  SDA to A4
  SCL to A5
  ** Rain Sensor **
  5V to 5V or Vcc
  GND to GND
  AO to A2
  DO to D2
  ** Temperature **
  5V to 5V or Vcc
  GND to GND
  White/Blue to D3

custom parts:
  LM2596: LM2596 switching voltage regulator
  solar_pannel: Solar pannel
  YL-83 Rain Sensor - Control Board: The YL-83 is a rain sensor that has more resistance when dry and less resistance when wet. The module runs at 5V.
  YL-83 Rain Sensor - Detection Board: The YL-83 is a rain sensor that has more resistance when dry and less resistance when wet. The module runs at 5V.
