# Fritzing sketch Sketch09-pro_mini-chuva-temperatura-RTC-SD-sem_RF24 (saved by Fritzing 0.9.2b)
breadboards: 1

parts:
  LM1 = LM2596 [package=multiwatt15]
  Solar_pannel1 = solar_pannel
  YL-83_-_Control_Board2 = YL-83 Rain Sensor - Control Board
  YL-83_-_Detection_Board2 = YL-83 Rain Sensor - Detection Board
  DS3 = DS18B20 1-Wire Temperature Sensor Probe Cable
  Part4 = MicroSD Card Module
  Arduino1 = Arduino Pro Mini v13
  VCC2 = 4 x AAA Battery Mount
  ZS-042_RTC3 = ZS-042 RTC Module
  D5 = Rectifier Diode [part_number=1N4342 package="300 mil [THT]"]
  R5 = Resistor [tolerance=±5% resistance=4.7k package=THT]
  D6 = Rectifier Diode [part_number=1N4342 package="300 mil [THT]"]
  R6 = Resistor [tolerance=±5% resistance=4.7k package=THT]

nets:
  N1: LM1.Vin, Solar_pannel1.aún_sin_nombre#1
  N2: LM1.GND, Solar_pannel1.aún_sin_nombre#0
  VCC: YL-83_-_Control_Board2.VCC, DS3.VDD, Part4.VCC, Arduino1.VCC, ZS-042_RTC3.VCC
  GND: YL-83_-_Control_Board2.GND, DS3.GND, Part4.GND, VCC2.-, ZS-042_RTC3.GND, R5.Pin_1, R6.Pin_1
  N3: YL-83_-_Control_Board2.DO, Arduino1.D2
  N4: YL-83_-_Control_Board2.AO, Arduino1.A2
  N5: YL-83_-_Control_Board2.POS, YL-83_-_Detection_Board2.POS
  N6: YL-83_-_Control_Board2.NEG, YL-83_-_Detection_Board2.NEG
  N7: DS3.DQ, Arduino1.D3_PWM
  N8: Part4.MISO, Arduino1.D12/MISO
  N9: Part4.MOSI, Arduino1.D11_PWM/MOSI
  N10: Part4.SCK, Arduino1.D13/SCK
  N11: Part4.CS, Arduino1.D10_PWM/SS
  N12: Arduino1.A4, ZS-042_RTC3.SDA
  N13: Arduino1.A5, ZS-042_RTC3.SCL
  N14: Arduino1.RAW, VCC2.+
  N15: Arduino1.A1, D6.cathode, R6.Pin_0
  N16: Arduino1.A0, D5.cathode, R5.Pin_0
  N17: Arduino1.D7, D6.anode
  N18: Arduino1.D6_PWM, D5.anode

notes:
  ** Micro SD **
  5V to 5V or Vcc
  GND to GND
  D13 to SCK
  D12 to MOSI
  D11 to MISO
  D10 to CS
  (sim, MISO e MOSI estão 'invertidos')
  ** RTC **
  5V to 5V or Vcc
  GND to GND
  SDA to A4
  SCL to A5
  ** Rain Sensor **
  5V to 5V or Vcc
  GND to GND
  AO to A2
  DO to D2
  ** Temperature **
  5V to 5V or Vcc
  GND to GND
  White/Blue to D3

custom parts:
  LM2596: LM2596 switching voltage regulator
  solar_pannel: Solar pannel
  YL-83 Rain Sensor - Control Board: The YL-83 is a rain sensor that has more resistance when dry and less resistance when wet. The module runs at 5V.
  YL-83 Rain Sensor - Detection Board: The YL-83 is a rain sensor that has more resistance when dry and less resistance when wet. The module runs at 5V.
