# Fritzing sketch Sketch10-pro_mini-RTC-SD-3WM (saved by Fritzing 0.9.2b)
breadboards: 1

parts:
  Part4 = MicroSD Card Module
  Arduino1 = Arduino Pro Mini v13
  VCC2 = 4 x AAA Battery Mount
  ZS-042_RTC3 = ZS-042 RTC Module
  J1 = screw terminal, 2 pins
  R8 = Resistor [tolerance=±5% resistance=4.7k package=THT]
  D6 = Rectifier Diode [part_number=1N4342 package="300 mil [THT]"]
  D7 = Rectifier Diode [part_number=1N4342 package="300 mil [THT]"]
  R9 = Resistor [tolerance=±5% resistance=4.7k package=THT]

nets:
  GND: Part4.GND, VCC2.-, ZS-042_RTC3.GND
  VCC: Part4.VCC, Arduino1.VCC, ZS-042_RTC3.VCC
  N1: Part4.MISO, Arduino1.D12/MISO
  N2: Part4.MOSI, Arduino1.D11_PWM/MOSI
  N3: Part4.SCK, Arduino1.D13/SCK
  N4: Part4.CS, Arduino1.D10_PWM/SS
  N5: Arduino1.A4, ZS-042_RTC3.SDA
  N6: Arduino1.A5, ZS-042_RTC3.SCL
  N7: Arduino1.RAW, VCC2.+
  N8: Arduino1.A1, J1.pin2, D7.cathode, R9.Pin_1
  N9: Arduino1.A0, J1.pin1, R8.Pin_1, D6.cathode
  N10: Arduino1.D5_PWM, D7.anode
  N11: Arduino1.D4, D6.anode
  N12: R8.Pin_0, R9.Pin_0

notes:
  ** Micro SD **
  5V to 5V or Vcc
  GND to GND
  D13 to SCK
  D12 to MOSI
  D11 to MISO
  D10 to CS
  (sim, MISO e MOSI estão 'invertidos')
  ** RTC **
  5V to 5V or Vcc
  GND to GND
  SDA to A4
  SCL to A5
