# Fritzing sketch chip-temperature (saved by Fritzing 0.9.3b)
breadboards: 1

parts:
  C_H_I_P_1 = Next Thing Co. C.H.I.P
  DS4 = DS18B20 1-Wire Temperature Sensor Probe Cable
  R1 = Resistor [tolerance=±5% resistance=4.7k package="0805 [SMD]"]
  Part1 = NRF24L01+ Breakout Board
  YL-83_-_Control_Board3 = YL-83 Rain Sensor - Control Board
  YL-83_-_Detection_Board3 = YL-83 Rain Sensor - Detection Board

nets:
  VCC: C_H_I_P_1.VCC-3V3#5, DS4.VDD, Part1.VCC, YL-83_-_Control_Board3.VCC
  N1: C_H_I_P_1.LCD-D2, DS4.DQ, R1.Pin_0
  N2: C_H_I_P_1.VCC-3V3#49, Part1.CE
  N3: C_H_I_P_1.XIO-P0, YL-83_-_Control_Board3.DO
  N4: C_H_I_P_1.CSIPCK, Part1.CS
  N5: C_H_I_P_1.CSICK, Part1.SCK
  N6: C_H_I_P_1.CSIHSYNC, Part1.MOSI
  N7: C_H_I_P_1.CSIVSYNC, Part1.MISO
  GND: C_H_I_P_1.GND, DS4.GND, Part1.GND, YL-83_-_Control_Board3.GND
  N8: YL-83_-_Control_Board3.POS, YL-83_-_Detection_Board3.POS
  N9: YL-83_-_Control_Board3.NEG, YL-83_-_Detection_Board3.NEG

notes:
  ** Rain Sensor **
  3.3v or 5V to VCC
  GND to GND
  AO to ?
  DO to XIO-P0

custom parts:
  YL-83 Rain Sensor - Control Board: The YL-83 is a rain sensor that has more resistance when dry and less resistance when wet. The module runs at 5V.
  YL-83 Rain Sensor - Detection Board: The YL-83 is a rain sensor that has more resistance when dry and less resistance when wet. The module runs at 5V.
