# Fritzing sketch teste2 (saved by Fritzing 0.9.2b)
breadboards: 1

parts:
  LM1 = LM2596 [package=multiwatt15]
  Solar_pannel1 = solar_pannel
  YL-83_-_Control_Board2 = YL-83 Rain Sensor - Control Board
  YL-83_-_Detection_Board2 = YL-83 Rain Sensor - Detection Board
  DS3 = DS18B20 1-Wire Temperature Sensor Probe Cable  # not connected
  Part3 = Arduino Cellular Shield
  Part5 = Arduino Nano (Rev3.0)
  VCC1 = 4 x AAA Battery Mount
  D3 = Rectifier Diode [part_number=1N4342 package="300 mil [THT]"]
  R3 = Resistor [tolerance=±5% resistance=4.7k package=THT]
  D4 = Rectifier Diode [part_number=1N4342 package="300 mil [THT]"]
  R4 = Resistor [tolerance=±5% resistance=4.7k package=THT]
  Part6 = NRF24L01  # not connected
  Part7 = Arduino Uno (Rev3)  # not connected
  Arduino1 = Arduino Pro Mini v13  # not connected

nets:
  N1: LM1.Vin, Solar_pannel1.aún_sin_nombre#1
  N2: LM1.GND, Solar_pannel1.aún_sin_nombre#0
  N3: YL-83_-_Control_Board2.POS, YL-83_-_Detection_Board2.POS
  N4: YL-83_-_Control_Board2.NEG, YL-83_-_Detection_Board2.NEG
  5V: Part3.5V, Part5.5V
  GND: Part3.GND, Part5.GND, VCC1.-, R3.Pin_1, R4.Pin_0
  N5: Part3.RX-I, Part5.D1/TX
  N6: Part3.TX-O, Part5.D0/RX
  N7: Part5.D6, D4.anode
  N8: Part5.D7, D3.anode
  N9: Part5.VIN, VCC1.+
  N10: Part5.A1, D3.cathode, R3.Pin_0
  N11: Part5.A0, D4.cathode, R4.Pin_1

notes:
  ** Rain Sensor **
  5V to 5V or Vcc
  GND to GND
  AO to A2
  DO to D2
  ** Temperature **
  5V to 5V or Vcc
  GND to GND
  White/Blue to D3

custom parts:
  LM2596: LM2596 switching voltage regulator
  solar_pannel: Solar pannel
  YL-83 Rain Sensor - Control Board: The YL-83 is a rain sensor that has more resistance when dry and less resistance when wet. The module runs at 5V.
  YL-83 Rain Sensor - Detection Board: The YL-83 is a rain sensor that has more resistance when dry and less resistance when wet. The module runs at 5V.
