# Fritzing sketch teste3b (saved by Fritzing 0.9.2b)
circuit board: 8.46667cm x 5.64444cm
perfboards: 1

parts:
  R1 = Resistor [tolerance=±5% resistance=4.7k package=THT]
  R2 = Resistor [tolerance=±5% resistance=4.7k package=THT]
  R3 = Resistor [tolerance=±5% resistance=4.7k package=THT]
  D3 = Rectifier Diode [part_number=1N4342 package="300 mil [THT]"]
  D4 = Rectifier Diode [part_number=1N4342 package="300 mil [THT]"]
  R4 = Resistor [tolerance=±5% resistance=4.7k package=THT]
  D6 = Resistor [tolerance=±5% resistance=4.7k package=THT]
  R5 = Resistor [tolerance=±5% resistance=4.7k package=THT]
  D5 = Rectifier Diode [part_number=1N4342 package="300 mil [THT]"]
  R6 = Rectifier Diode [part_number=1N4342 package="300 mil [THT]"]
  D1 = Rectifier Diode [part_number=1N4342 package="300 mil [THT]"]
  D2 = Rectifier Diode [part_number=1N4342 package="300 mil [THT]"]
  Arduino_Pro_Mini = Arduino Pro Mini v13
  Part5 = MicroSD Card Module

nets:
  N1: R1.Pin_0, R2.Pin_0, R3.Pin_0, R4.Pin_0, D6.Pin_0, R5.Pin_0, Arduino_Pro_Mini.GND
  N2: R1.Pin_1, D1.cathode, Arduino_Pro_Mini.A0
  N3: R2.Pin_1, D2.cathode, Arduino_Pro_Mini.A1
  N4: R3.Pin_1, D3.anode, Arduino_Pro_Mini.A2
  N5: D3.cathode, Arduino_Pro_Mini.D6_PWM
  N6: D4.cathode, Arduino_Pro_Mini.D7
  N7: D4.anode, R4.Pin_1, Arduino_Pro_Mini.A3
  N8: D6.Pin_1, R6.anode, Arduino_Pro_Mini.A5
  N9: R5.Pin_1, D5.anode, Arduino_Pro_Mini.A4
  N10: D5.cathode, Arduino_Pro_Mini.D8
  N11: R6.cathode, Arduino_Pro_Mini.D9_PWM
  N12: D1.anode, Arduino_Pro_Mini.D4
  N13: D2.anode, Arduino_Pro_Mini.D5_PWM
  VCC: Arduino_Pro_Mini.VCC, Part5.VCC
  N14: Arduino_Pro_Mini.D13/SCK, Part5.SCK
  N15: Arduino_Pro_Mini.D12/MISO, Part5.MISO
  N16: Arduino_Pro_Mini.D11_PWM/MOSI, Part5.MOSI
  N17: Arduino_Pro_Mini.D10_PWM/SS, Part5.CS

notes:
  ** Micro SD **
  5V to 5V or Vcc
  GND to GND
  D13 to SCK
  D12 to MISO
  D11 to MOSI
  D10 to CS
