# Fritzing sketch teste3c (saved by Fritzing 0.9.2b)
breadboards: 2
perfboards: 1

parts:
  LM1 = LM2596 [package=multiwatt15]
  Solar_pannel1 = solar_pannel
  YL-83_-_Detection_Board2 = YL-83 Rain Sensor - Detection Board  # not connected
  DS3 = DS18B20 1-Wire Temperature Sensor Probe Cable
  Arduino1 = Arduino Pro Mini v13
  D5 = Rectifier Diode [part_number=1N4342 package="300 mil [THT]"]
  R5 = Resistor [tolerance=±5% resistance=4.7k package=THT]
  D6 = Rectifier Diode [part_number=1N4342 package="300 mil [THT]"]
  R6 = Resistor [tolerance=±5% resistance=4.7k package=THT]
  D7 = Rectifier Diode [part_number=1N4342 package="300 mil [THT]"]
  R7 = Resistor [tolerance=±5% resistance=4.7k package=THT]
  Arduino2 = Arduino Pro Mini v13
  D8 = Rectifier Diode [part_number=1N4342 package="300 mil [THT]"]
  R8 = Resistor [tolerance=±5% resistance=4.7k package=THT]
  D9 = Rectifier Diode [part_number=1N4342 package="300 mil [THT]"]
  R9 = Resistor [tolerance=±5% resistance=4.7k package=THT]
  D10 = Rectifier Diode [part_number=1N4342 package="300 mil [THT]"]
  R10 = Resistor [tolerance=±5% resistance=4.7k package=THT]
  R11 = Resistor [tolerance=±5% resistance=4.7k package=THT]  # not connected
  D11 = Rectifier Diode [part_number=1N4342 package="300 mil [THT]"]  # not connected
  D12 = Rectifier Diode [part_number=1N4342 package="300 mil [THT]"]  # not connected
  R12 = Resistor [tolerance=±5% resistance=4.7k package=THT]  # not connected
  Arduino3 = Arduino Pro Mini v13
  J1 = screw terminal, 2 pins  # not connected
  J2 = screw terminal, 2 pins  # not connected
  J3 = screw terminal, 2 pins  # not connected
  JP1 = Header 12 [package=1x12_machine-pin-header_lock.004]  # not connected
  JP2 = Header 10 [package=1x10-2mm-smd]

nets:
  N1: LM1.Vin, Solar_pannel1.aún_sin_nombre#1
  N2: LM1.GND, Solar_pannel1.aún_sin_nombre#0
  N3: DS3.GND, R5.Pin_1, R6.Pin_1
  N4: DS3.DQ, Arduino1.D3_PWM
  VDD: DS3.VDD, Arduino1.VCC
  N5: Arduino1.A1, D6.cathode, R6.Pin_0
  N6: Arduino1.A0, D5.cathode, R5.Pin_0
  N7: Arduino1.D7, D6.anode
  N8: Arduino1.D6_PWM, D5.anode
  N9: D7.cathode, R7.Pin_0, Arduino2.A0
  N10: D7.anode, Arduino2.D4
  N11: R7.Pin_1, R8.Pin_0
  N12: Arduino2.A1, D8.cathode, R8.Pin_1
  N13: Arduino2.D5_PWM, D8.anode
  N14: D9.cathode, R9.Pin_0
  N15: R9.Pin_1, R10.Pin_1
  N16: D10.cathode, R10.Pin_0
  N17: Arduino3.GND, JP2.10

notes:
  ** Micro SD **
  5V to 5V or Vcc
  GND to GND
  D13 to SCK
  D12 to MISO
  D11 to MOSI
  D10 to CS
  ** RTC **
  5V to 5V or Vcc
  GND to GND
  SDA to A4
  SCL to A5
  ** Rain Sensor **
  5V to 5V or Vcc
  GND to GND
  AO to A2
  DO to D2
  ** Temperature **
  5V to 5V or Vcc
  GND to GND
  White/Blue to D3

custom parts:
  LM2596: LM2596 switching voltage regulator
  solar_pannel: Solar pannel
  YL-83 Rain Sensor - Detection Board: The YL-83 is a rain sensor that has more resistance when dry and less resistance when wet. The module runs at 5V.
