# Fritzing sketch Sketch04 (saved by Fritzing 0.9.3b)
breadboards: 1

parts:
  Componente1 = Arduino Uno (Rev3)
  R1 = Resistor [tolerance=±5% resistance=4.7k package=THT]
  R2 = Resistor [tolerance=±5% resistance=4.7k package=THT]
  D1 = Rectifier Diode [part_number=1N4342 package="300 mil [THT]"]
  D2 = Rectifier Diode [part_number=1N4342 package="300 mil [THT]"]
  Part1 = NRF24L01+ Breakout Board
  ZS-042_RTC1 = ZS-042 RTC Module

nets:
  N1: Componente1.A0, R1.Pin_0, D2.cathode
  N2: Componente1.A1, R2.Pin_1, D1.cathode
  N3: Componente1.A4/SDA, ZS-042_RTC1.SDA
  N4: Componente1.A5/SCL, ZS-042_RTC1.SCL
  N5: Componente1.D8, Part1.CE
  N6: Componente1.D9_PWM, Part1.CS
  N7: Componente1.D11_PWM/MOSI, Part1.MOSI
  N8: Componente1.D12/MISO, Part1.MISO
  N9: Componente1.D13/SCK, Part1.SCK
  GND: Componente1.GND, R1.Pin_1, R2.Pin_0, Part1.GND, ZS-042_RTC1.GND
  N10: Componente1.D6_PWM, D2.anode
  N11: Componente1.D7, D1.anode
  3V3: Componente1.3V3, Part1.VCC
  5V: Componente1.5V, ZS-042_RTC1.VCC
